// Logisim project CPU.circ as structural Verilog: 7 circuits, main circuit MCU
module MCU (
  input  IN_ENABLE,
  input  [7:0] IN,
  input  CLK,
  input  RST,
  output [7:0] ADDR,
  output [7:0] OUT
);

  wire alu_1_flag, and_1_out, isd_1_a_mux, isd_1_compare, isd_1_jmp, isd_1_out_16, isd_1_pop, isd_1_push;
  wire [1:0] isd_1_a, isd_1_b, isd_1_c, isd_1_gpr_mux;
  wire [2:0] isd_1_out_9;
  wire [3:0] isd_1_aux_op;
  wire [7:0] gpr_1_out_7, gpr_1_out_8, isd_1_imm_value, isd_1_mem_pointer, multiplexer_2_out,
       multiplexer_3_out, pc_1_out_6, pc_1_out_7, ram_1_data, stk_1_out_6;

  STK stk_1 (.out_6(stk_1_out_6), .in_1(OUT), .in_2(CLK), .in_4(isd_1_pop), .in_5(isd_1_push), .in_3(RST));
  ISD isd_1 (
    .in_1(multiplexer_3_out), .CLK(CLK), .RST(RST), .out_9(isd_1_out_9), .GPR_MUX(isd_1_gpr_mux),
    .A_MUX(isd_1_a_mux), .POP(isd_1_pop), .PUSH(isd_1_push), .A(isd_1_a), .B(isd_1_b), .C(isd_1_c),
    .out_16(isd_1_out_16), .JMP(isd_1_jmp), .JMP_FLAG(alu_1_flag), .ALU(OUT),
    .MEM_POINTER(isd_1_mem_pointer), .CUR_PC_ADDR(pc_1_out_7), .IMM_VALUE(isd_1_imm_value),
    .AUX_OP(isd_1_aux_op), .COMPARE(isd_1_compare));
  PC pc_1 (
    .Jump_Address(multiplexer_3_out), .Jump_Enable(isd_1_jmp), .out_6(pc_1_out_6), .in_5(RST),
    .out_7(pc_1_out_7), .in_3(isd_1_a_mux), .in_4(CLK));
  Multiplexer #(.width(8), .enable("false")) multiplexer_1 (
    .in0(pc_1_out_6), .in1(isd_1_mem_pointer), .out(ADDR), .sel(isd_1_a_mux));
  Multiplexer #(.select(2), .width(8), .enable("false")) multiplexer_2 (
    .in0(OUT), .in1(multiplexer_3_out), .in2(stk_1_out_6), .in3(isd_1_imm_value), .out(multiplexer_2_out),
    .sel(isd_1_gpr_mux));
  ALU alu_1 (
    .Opcodes(OUT), .OPCODE(isd_1_out_9), .in_1(gpr_1_out_7), .in_2(gpr_1_out_8), .FLAG(alu_1_flag),
    .AUX_OP(isd_1_aux_op), .COMPARE_ENABLE(isd_1_compare));
  GPR gpr_1 (
    .in_2(isd_1_c), .in_3(multiplexer_2_out), .out_7(gpr_1_out_7), .out_8(gpr_1_out_8), .in_5(isd_1_b),
    .in_6(isd_1_a), .in_1(CLK), .in_4(RST));
  and and_1 (and_1_out, CLK, isd_1_out_16);
  Multiplexer #(.width(8), .enable("false")) multiplexer_3 (
    .in0(ram_1_data), .in1(IN), .out(multiplexer_3_out), .sel(IN_ENABLE));
  RAM #(.bus("separate")) ram_1 (
    .addr(ADDR), .din(OUT), .data(ram_1_data), .sel(1'b1), .clk(and_1_out));  // open: str, ld, clr

  // Notes on the sheet:
  //   ADDR: pull=down
  //   OUT: pull=down
  //   IN: pull=down
  //   IN_ENABLE: pull=down
  //   CLK: pull=down
  //   RST: pull=down
  //   TISCv1.0
endmodule

module ALU (
  input  [7:0] in_1,
  input  [7:0] in_2,
  input  [2:0] OPCODE,
  input  COMPARE_ENABLE,
  input  [3:0] AUX_OP,
  output [7:0] Opcodes,
  output FLAG
);

  wire and_1_out, and_2_out, and_3_out, and_4_out, and_5_out, and_6_out, and_7_out, and_8_out, and_9_out,
       and_10_out, and_11_out, and_12_out, and_13_out, and_14_out, and_15_out, and_16_out, and_17_out,
       and_18_out, and_19_out, and_20_out, and_21_out, and_22_out, and_23_out, and_24_out, and_25_out,
       and_26_out, and_27_out, and_28_out, and_29_out, and_30_out, and_31_out, and_32_out, CC, CI, FC, nA,
       nB, nor_1_out, nor_2_out, nor_3_out, nor_4_out, nor_5_out, nor_6_out, nor_7_out, nor_8_out, OR,
       or_1_out, or_2_out, or_3_out, or_4_out, or_5_out, or_6_out, or_7_out, or_8_out, or_9_out, or_10_out,
       or_11_out, or_12_out, or_13_out, or_14_out, or_15_out, or_16_out, or_17_out, or_18_out, or_19_out,
       or_20_out, or_21_out, or_22_out, or_23_out, or_24_out, or_25_out, xor_1_out, xor_2_out, xor_3_out,
       xor_4_out, xor_5_out, xor_6_out, xor_7_out, xor_8_out, xor_9_out, xor_10_out, xor_11_out, xor_12_out,
       xor_13_out, xor_14_out, xor_15_out, xor_16_out;
  wire [2:0] multiplexer_2_out, rom_1_data;
  wire [3:3] rom_1_data_2;

  xor xor_1 (xor_1_out, in_1[0], nB);
  xor xor_2 (xor_2_out, in_2[0], nA);
  xor xor_3 (xor_3_out, in_1[1], nB);
  xor xor_4 (xor_4_out, in_2[1], nA);
  xor xor_5 (xor_5_out, in_1[2], nB);
  xor xor_6 (xor_6_out, in_2[2], nA);
  xor xor_7 (xor_7_out, in_1[3], nB);
  xor xor_8 (xor_8_out, in_2[3], nA);
  xor xor_9 (xor_9_out, in_1[4], nB);
  xor xor_10 (xor_10_out, in_2[4], nA);
  xor xor_11 (xor_11_out, in_1[5], nB);
  xor xor_12 (xor_12_out, in_2[5], nA);
  xor xor_13 (xor_13_out, in_1[6], nB);
  xor xor_14 (xor_14_out, in_2[6], nA);
  xor xor_15 (xor_15_out, in_1[7], nB);
  xor xor_16 (xor_16_out, in_2[7], nA);
  nor nor_1 (nor_1_out, xor_1_out, xor_2_out);
  or or_1 (or_1_out, nor_1_out, and_2_out);
  and and_1 (and_1_out, xor_1_out, xor_2_out);
  and and_2 (and_2_out, and_1_out, ~OR);  // AND_Gate
  and and_3 (and_3_out, and_2_out, ~CC);  // AND_Gate
  or or_2 (or_2_out, and_25_out, FC);
  or or_3 (or_3_out, and_3_out, or_2_out);
  nor nor_2 (nor_2_out, xor_3_out, xor_4_out);
  or or_4 (or_4_out, nor_2_out, and_5_out);
  and and_4 (and_4_out, xor_3_out, xor_4_out);
  and and_5 (and_5_out, and_4_out, ~OR);  // AND_Gate
  and and_6 (and_6_out, and_5_out, ~CC);  // AND_Gate
  or or_5 (or_5_out, and_26_out, FC);
  or or_6 (or_6_out, and_6_out, or_5_out);
  nor nor_3 (nor_3_out, xor_5_out, xor_6_out);
  or or_7 (or_7_out, nor_3_out, and_8_out);
  and and_7 (and_7_out, xor_5_out, xor_6_out);
  and and_8 (and_8_out, and_7_out, ~OR);  // AND_Gate
  or or_8 (or_8_out, and_27_out, FC);
  and and_9 (and_9_out, and_8_out, ~CC);  // AND_Gate
  or or_9 (or_9_out, and_9_out, or_8_out);
  nor nor_4 (nor_4_out, xor_7_out, xor_8_out);
  or or_10 (or_10_out, nor_4_out, and_11_out);
  and and_10 (and_10_out, xor_7_out, xor_8_out);
  and and_11 (and_11_out, and_10_out, ~OR);  // AND_Gate
  or or_11 (or_11_out, and_28_out, FC);
  and and_12 (and_12_out, and_11_out, ~CC);  // AND_Gate
  or or_12 (or_12_out, and_12_out, or_11_out);
  nor nor_5 (nor_5_out, xor_9_out, xor_10_out);
  or or_13 (or_13_out, nor_5_out, and_14_out);
  and and_13 (and_13_out, xor_9_out, xor_10_out);
  and and_14 (and_14_out, and_13_out, ~OR);  // AND_Gate
  and and_15 (and_15_out, and_14_out, ~CC);  // AND_Gate
  or or_14 (or_14_out, and_29_out, FC);
  or or_15 (or_15_out, and_15_out, or_14_out);
  nor nor_6 (nor_6_out, xor_11_out, xor_12_out);
  or or_16 (or_16_out, nor_6_out, and_17_out);
  and and_16 (and_16_out, xor_11_out, xor_12_out);
  and and_17 (and_17_out, and_16_out, ~OR);  // AND_Gate
  or or_17 (or_17_out, and_30_out, FC);
  and and_18 (and_18_out, and_17_out, ~CC);  // AND_Gate
  or or_18 (or_18_out, and_18_out, or_17_out);
  nor nor_7 (nor_7_out, xor_13_out, xor_14_out);
  or or_19 (or_19_out, nor_7_out, and_20_out);
  and and_19 (and_19_out, xor_13_out, xor_14_out);
  and and_20 (and_20_out, and_19_out, ~OR);  // AND_Gate
  and and_21 (and_21_out, and_20_out, ~CC);  // AND_Gate
  or or_20 (or_20_out, and_31_out, FC);
  or or_21 (or_21_out, and_21_out, or_20_out);
  nor nor_8 (nor_8_out, xor_15_out, xor_16_out);
  or or_22 (or_22_out, nor_8_out, and_23_out);
  and and_22 (and_22_out, xor_15_out, xor_16_out);
  and and_23 (and_23_out, and_22_out, ~OR);  // AND_Gate
  or or_23 (or_23_out, and_32_out, FC);
  and and_24 (and_24_out, and_23_out, ~CC);  // AND_Gate
  or or_24 (or_24_out, and_24_out, or_23_out);
  Multiplexer #(.enable("false")) multiplexer_1 (.in0(or_24_out), .in1(or_25_out), .out(FLAG), .sel(rom_1_data_2[3]));
  xnor xnor_1 (Opcodes[0], CI, or_1_out);
  and and_25 (and_25_out, CI, ~or_1_out);  // AND_Gate
  xnor xnor_2 (Opcodes[1], or_3_out, or_4_out);
  and and_26 (and_26_out, or_3_out, ~or_4_out);  // AND_Gate
  xnor xnor_3 (Opcodes[2], or_6_out, or_7_out);
  and and_27 (and_27_out, or_6_out, ~or_7_out);  // AND_Gate
  xnor xnor_4 (Opcodes[3], or_9_out, or_10_out);
  and and_28 (and_28_out, or_9_out, ~or_10_out);  // AND_Gate
  xnor xnor_5 (Opcodes[4], or_12_out, or_13_out);
  and and_29 (and_29_out, or_12_out, ~or_13_out);  // AND_Gate
  xnor xnor_6 (Opcodes[5], or_15_out, or_16_out);
  and and_30 (and_30_out, or_15_out, ~or_16_out);  // AND_Gate
  xnor xnor_7 (Opcodes[6], or_18_out, or_19_out);
  and and_31 (and_31_out, or_18_out, ~or_19_out);  // AND_Gate
  xnor xnor_8 (Opcodes[7], or_21_out, or_22_out);
  and and_32 (and_32_out, or_21_out, ~or_22_out);  // AND_Gate
  Multiplexer #(.width(3), .enable("false")) multiplexer_2 (
    .in0(OPCODE), .in1(rom_1_data), .out(multiplexer_2_out), .sel(COMPARE_ENABLE));
  ROM #(.addrWidth(4), .dataWidth(4)) rom_1 (.addr(AUX_OP), .data({rom_1_data_2[3], rom_1_data}));  // open: sel
  ROM #(.addrWidth(3), .dataWidth(6)) rom_2 (.addr(multiplexer_2_out), .data({nA, nB, OR, CC, CI, FC}), .sel(1'b1));
  or or_25 (or_25_out, Opcodes[0], Opcodes[1], Opcodes[2], Opcodes[3], Opcodes[4], Opcodes[5], Opcodes[6], Opcodes[7]);

  // Other names for the same wires on the sheet: b0 = in_1[0]; b1 = in_1[1]; b2 = in_1[2]; b3 = in_1[3]; b4 = in_1[4];
  //   b5 = in_1[5]; b6 = in_1[6]; b7 = in_1[7]; a0 = in_2[0]; a1 = in_2[1]; a2 = in_2[2]; a3 = in_2[3]; a4 = in_2[4];
  //   a5 = in_2[5]; a6 = in_2[6]; a7 = in_2[7]; o0 = Opcodes[0]; o1 = Opcodes[1]; o2 = Opcodes[2]; o3 = Opcodes[3];
  //   o4 = Opcodes[4]; o5 = Opcodes[5]; o6 = Opcodes[6]; o7 = Opcodes[7]

  // Notes on the sheet:
  //   Input B
  //   Output
  //   contents of rom_1 (hex, n*v repeats v):
  //   7 3 9 d a
  //   Input A
  //   contents of rom_2 (hex, n*v repeats v):
  //   8 3b 4 0 2 38 7 12
  //   OPCODES: 000: OR, 001: AND, 010: XOR, 011: ADD, 100: CIN, 101: NAND, 110: XNOR, 111: SUB
endmodule

module GPR (
  input  in_1,
  input  [1:0] in_2,
  input  [7:0] in_3,
  input  in_4,
  input  [1:0] in_5,
  input  [1:0] in_6,
  output [7:0] out_7,
  output [7:0] out_8
);

  wire decoder_1_out0, decoder_1_out1, decoder_1_out2, decoder_1_out3, decoder_2_out1, decoder_2_out2,
       decoder_2_out3, decoder_3_out0, decoder_3_out1, decoder_3_out2, decoder_3_out3;
  wire [1:0] multiplexer_1_out;
  wire [7:0] register_1_q, register_2_q, register_3_q;

  Multiplexer #(.width(2), .enable("false")) multiplexer_1 (
    .in0(2'b00), .in1(in_2), .out(multiplexer_1_out), .sel(in_1));
  Decoder #(.select(2), .enable("false")) decoder_1 (
    .out0(decoder_1_out0), .out1(decoder_1_out1), .out2(decoder_1_out2), .out3(decoder_1_out3), .sel(in_5));
  Decoder #(.select(2), .enable("false")) decoder_2 (
    .out1(decoder_2_out1), .out2(decoder_2_out2), .out3(decoder_2_out3), .sel(multiplexer_1_out));  // open: out0
  Register register_1 (.D(in_3), .en(1'b1), .Q(register_1_q), .clk(decoder_2_out2), .clr(in_4));
  Register register_2 (.D(in_3), .en(1'b1), .Q(register_2_q), .clk(decoder_2_out1), .clr(in_4));
  assign out_7 = decoder_1_out1 ? register_2_q : 8'bz;  // Controlled_Buffer controlled_buffer_1
  assign out_7 = decoder_1_out2 ? register_1_q : 8'bz;  // Controlled_Buffer controlled_buffer_2
  assign out_8 = decoder_3_out2 ? register_1_q : 8'bz;  // Controlled_Buffer controlled_buffer_3
  assign out_8 = decoder_3_out1 ? register_2_q : 8'bz;  // Controlled_Buffer controlled_buffer_4
  Register register_3 (.D(in_3), .en(1'b1), .Q(register_3_q), .clk(decoder_2_out3), .clr(in_4));
  assign out_7 = decoder_1_out3 ? register_3_q : 8'bz;  // Controlled_Buffer controlled_buffer_5
  assign out_7 = decoder_1_out0 ? {8{1'b0}} : 8'bz;  // Controlled_Buffer controlled_buffer_6
  assign out_8 = decoder_3_out3 ? register_3_q : 8'bz;  // Controlled_Buffer controlled_buffer_7
  assign out_8 = decoder_3_out0 ? {8{1'b0}} : 8'bz;  // Controlled_Buffer controlled_buffer_8
  Decoder #(.select(2), .enable("false")) decoder_3 (
    .out0(decoder_3_out0), .out1(decoder_3_out1), .out2(decoder_3_out2), .out3(decoder_3_out3), .sel(in_6));
endmodule

module ISD (
  input  [7:0] in_1,
  input  CLK,
  input  RST,
  input  [7:0] ALU,
  input  [7:0] CUR_PC_ADDR,
  input  JMP_FLAG,
  output COMPARE,
  output [3:0] AUX_OP,
  output [2:0] out_9,
  output [1:0] GPR_MUX,
  output POP,
  output PUSH,
  output [1:0] A,
  output [1:0] B,
  output [1:0] C,
  output out_16,
  output [7:0] MEM_POINTER,
  output [7:0] IMM_VALUE,
  output A_MUX,
  output JMP
);

  wire ADD_out, and_1_out, and_3_out, CIN_out, JMP_out, LB_out, LLI_out, LUI_out, NAND_out, or_1_out,
       or_2_out, OR_4_out, or_5_out, or_6_out, or_7_out, or_8_out, or_9_out, or_10_out, or_11_out, or_12_out,
       or_13_out, or_14_out, or_15_out, or_16_out, or_17_out, or_18_out, or_20_out, or_21_out, or_22_out,
       or_23_out, or_24_out, or_25_out, or_26_out, or_27_out, or_28_out, or_29_out, or_30_out, or_31_out,
       or_32_out, or_33_out, or_34_out, or_35_out, or_36_out, or_37_out, or_38_out, or_39_out, or_40_out,
       or_41_out, or_42_out, or_43_out, or_44_out, or_45_out, or_46_out, or_47_out, or_50_out, or_51_out,
       or_52_out, or_53_out, or_54_out, or_55_out, or_56_out, or_57_out, or_58_out, or_59_out, or_60_out,
       or_61_out, or_62_out, or_63_out, or_64_out, or_65_out, or_66_out, or_67_out, or_68_out, or_69_out,
       or_70_out, or_71_out, or_72_out, or_73_out, or_74_out, or_75_out, or_76_out, or_77_out, or_78_out,
       or_79_out, or_80_out, or_81_out, or_82_out, or_83_out, or_84_out, or_85_out, or_86_out, or_87_out,
       or_88_out, or_89_out, or_90_out, or_91_out, or_92_out, or_93_out, or_94_out, or_95_out, or_96_out,
       or_97_out, or_98_out, or_99_out, or_100_out, or_101_out, or_102_out, or_103_out, or_104_out,
       or_105_out, or_106_out, or_107_out, or_108_out, or_110_out, or_111_out, or_112_out, or_113_out,
       or_114_out, or_115_out, or_116_out, or_117_out, or_118_out, or_119_out, or_120_out, or_121_out,
       or_122_out, or_123_out, or_124_out, or_125_out, or_126_out, or_127_out, or_128_out, or_129_out,
       or_130_out, or_131_out, or_132_out, or_133_out, or_134_out, or_135_out, or_136_out, or_137_out,
       or_140_out, or_141_out, or_142_out, or_143_out, or_144_out, or_145_out, or_146_out, or_147_out,
       or_148_out, or_149_out, or_150_out, or_151_out, or_152_out, or_153_out, or_154_out, or_155_out,
       or_156_out, or_157_out, or_158_out, or_159_out, or_160_out, or_161_out, or_162_out, or_163_out,
       or_164_out, or_165_out, or_166_out, or_167_out, or_168_out, or_170_out, or_171_out, or_172_out,
       or_173_out, or_174_out, or_175_out, or_176_out, or_177_out, or_178_out, or_179_out, or_180_out,
       or_181_out, or_182_out, or_183_out, or_188_out, or_189_out, or_190_out, or_191_out, or_192_out,
       or_193_out, or_194_out, or_195_out, or_196_out, or_197_out, or_198_out, or_199_out, or_200_out,
       or_201_out, or_202_out, or_203_out, or_204_out, or_205_out, or_206_out, or_207_out, or_208_out,
       or_209_out, or_210_out, or_211_out, or_212_out, or_213_out, or_214_out, or_215_out, or_216_out,
       or_217_out, or_218_out, or_219_out, or_220_out, or_221_out, or_222_out, or_223_out, or_224_out,
       or_225_out, or_226_out, or_227_out, or_228_out, or_229_out, or_230_out, or_231_out, or_233_out,
       or_234_out, PCR_out, POP_out, PUSH_out, register_3_q, register_5_q, SB_out, SCO_out, SP_out;
  wire [1:0] controlled_buffer_1_out, controlled_buffer_2_out, controlled_buffer_3_out,
       controlled_buffer_4_out, controlled_buffer_5_out, controlled_buffer_6_out, controlled_buffer_7_out,
       controlled_buffer_8_out, controlled_buffer_9_out, controlled_buffer_10_out, controlled_buffer_11_out,
       controlled_buffer_12_out, controlled_buffer_13_out, controlled_buffer_14_out,
       controlled_buffer_15_out, controlled_buffer_16_out, controlled_buffer_17_out,
       controlled_buffer_18_out, controlled_buffer_19_out, controlled_buffer_20_out,
       controlled_buffer_21_out, controlled_buffer_22_out, controlled_buffer_23_out,
       controlled_buffer_24_out, controlled_buffer_25_out, controlled_buffer_26_out,
       controlled_buffer_27_out, controlled_buffer_28_out, controlled_buffer_29_out,
       controlled_buffer_30_out, controlled_buffer_31_out, controlled_buffer_32_out,
       controlled_buffer_33_out, controlled_buffer_34_out, controlled_buffer_35_out,
       controlled_buffer_36_out, controlled_buffer_37_out, controlled_buffer_38_out,
       controlled_buffer_39_out, controlled_buffer_40_out, controlled_buffer_41_out,
       controlled_buffer_42_out, controlled_buffer_43_out, controlled_buffer_44_out,
       controlled_buffer_45_out, multiplexer_2_out, multiplexer_3_out, multiplexer_4_out, multiplexer_7_out,
       multiplexer_8_out, multiplexer_9_out, multiplexer_10_out, multiplexer_11_out, multiplexer_12_out,
       multiplexer_13_out, multiplexer_14_out, multiplexer_15_out, multiplexer_16_out, multiplexer_17_out,
       multiplexer_18_out, multiplexer_19_out, multiplexer_20_out, multiplexer_21_out, multiplexer_22_out,
       multiplexer_23_out, multiplexer_24_out, multiplexer_25_out, multiplexer_26_out, multiplexer_27_out,
       multiplexer_28_out, multiplexer_29_out, multiplexer_30_out, multiplexer_31_out, multiplexer_32_out,
       multiplexer_33_out, multiplexer_34_out, multiplexer_35_out, multiplexer_36_out, multiplexer_37_out,
       multiplexer_38_out, multiplexer_39_out, multiplexer_40_out, multiplexer_41_out, multiplexer_42_out,
       multiplexer_43_out, multiplexer_44_out, multiplexer_45_out, multiplexer_46_out, multiplexer_47_out,
       multiplexer_48_out, multiplexer_49_out, multiplexer_50_out, multiplexer_51_out, multiplexer_52_out;
  wire [7:0] multiplexer_1_out, multiplexer_5_out, or_3_out, register_1_q;

  Register #(.trigger("falling")) register_1 (.D(in_1), .Q(register_1_q), .clk(CLK), .clr(RST));  // open: en
  Multiplexer #(.width(8), .enable("false")) multiplexer_1 (
    .in0(register_1_q), .in1({8{1'b0}}), .out(multiplexer_1_out), .sel(register_5_q));
  or or_1 (or_1_out, multiplexer_1_out[2], multiplexer_1_out[3]);
  or or_2 (or_2_out, multiplexer_1_out[2], multiplexer_1_out[3]);
  Multiplexer #(.width(2), .enable("false")) multiplexer_2 (
    .in0(2'b00), .in1(multiplexer_1_out[3:2]), .out(multiplexer_2_out), .sel(or_79_out));
  Multiplexer #(.width(2), .enable("false")) multiplexer_3 (
    .in0(2'b00), .in1(multiplexer_1_out[5:4]), .out(multiplexer_3_out), .sel(or_78_out));
  Multiplexer #(.width(2), .enable("false")) multiplexer_4 (
    .in0(2'b00), .in1(multiplexer_1_out[7:6]), .out(multiplexer_4_out), .sel(or_108_out));
  assign or_3_out = {multiplexer_1_out[5:2], 4'b0000} | ALU;  // OR_Gate or_3, 8 bits wide
  Register register_2 (.D(ALU), .Q(MEM_POINTER), .clk(and_1_out), .clr(RST));  // open: en
  and and_1 (and_1_out, or_216_out, CLK);
  and OR_4 (OR_4_out, ~multiplexer_1_out[0], ~multiplexer_1_out[1], 1'b1, or_1_out, 1'b1, 1'b1, 1'b1, 1'b1);  // AND_Gate
  or or_5 (or_5_out, 1'b0, 1'b0);
  and SCO (SCO_out, ~multiplexer_1_out[0], ~multiplexer_1_out[1], ~multiplexer_1_out[2], ~multiplexer_1_out[3], 1'b1, 1'b1, 1'b1, 1'b1);  // AND_Gate
  or or_6 (or_6_out, 1'b0, or_5_out);
  and NAND (NAND_out, multiplexer_1_out[0], ~multiplexer_1_out[1], 1'b1, 1'b1, 1'b1, 1'b1, 1'b1, 1'b1);  // AND_Gate
  or or_7 (or_7_out, NAND_out, or_6_out);
  and ADD (ADD_out, ~multiplexer_1_out[0], multiplexer_1_out[1], 1'b1, or_2_out, 1'b1, 1'b1, 1'b1, 1'b1);  // AND_Gate
  or or_8 (or_8_out, 1'b0, or_7_out);
  and CIN (CIN_out, ~multiplexer_1_out[0], multiplexer_1_out[1], ~multiplexer_1_out[2], ~multiplexer_1_out[3], 1'b1, 1'b1, 1'b1, 1'b1);  // AND_Gate
  or or_9 (or_9_out, CIN_out, or_8_out);
  and LLI (LLI_out, multiplexer_1_out[0], multiplexer_1_out[1], 1'b1, 1'b1, 1'b1, 1'b1, ~multiplexer_1_out[6], ~multiplexer_1_out[7]);  // AND_Gate
  or or_10 (or_10_out, 1'b0, or_9_out);
  and LUI (LUI_out, multiplexer_1_out[0], multiplexer_1_out[1], 1'b1, 1'b1, 1'b1, 1'b1, multiplexer_1_out[6], ~multiplexer_1_out[7]);  // AND_Gate
  or or_11 (or_11_out, 1'b0, or_10_out);
  and u_JMP (JMP_out, multiplexer_1_out[0], multiplexer_1_out[1], ~multiplexer_1_out[2], ~multiplexer_1_out[3], ~multiplexer_1_out[4], ~multiplexer_1_out[5], ~multiplexer_1_out[6], multiplexer_1_out[7]);  // AND_Gate
  or or_12 (or_12_out, 1'b0, or_11_out);
  and u_PUSH (PUSH_out, multiplexer_1_out[0], multiplexer_1_out[1], ~multiplexer_1_out[2], ~multiplexer_1_out[3], multiplexer_1_out[4], ~multiplexer_1_out[5], ~multiplexer_1_out[6], multiplexer_1_out[7]);  // AND_Gate
  or or_13 (or_13_out, 1'b0, or_12_out);
  and u_POP (POP_out, multiplexer_1_out[0], multiplexer_1_out[1], ~multiplexer_1_out[2], ~multiplexer_1_out[3], ~multiplexer_1_out[4], multiplexer_1_out[5], ~multiplexer_1_out[6], multiplexer_1_out[7]);  // AND_Gate
  or or_14 (or_14_out, 1'b0, or_13_out);
  and PCR (PCR_out, multiplexer_1_out[0], multiplexer_1_out[1], ~multiplexer_1_out[2], ~multiplexer_1_out[3], multiplexer_1_out[4], multiplexer_1_out[5], ~multiplexer_1_out[6], multiplexer_1_out[7]);  // AND_Gate
  or or_15 (or_15_out, 1'b0, or_14_out);
  and LB (LB_out, multiplexer_1_out[0], multiplexer_1_out[1], multiplexer_1_out[2], ~multiplexer_1_out[3], 1'b1, 1'b1, ~multiplexer_1_out[6], multiplexer_1_out[7]);  // AND_Gate
  or or_16 (or_16_out, 1'b0, or_15_out);
  and SB (SB_out, multiplexer_1_out[0], multiplexer_1_out[1], ~multiplexer_1_out[2], multiplexer_1_out[3], 1'b1, 1'b1, ~multiplexer_1_out[6], multiplexer_1_out[7]);  // AND_Gate
  or or_17 (or_17_out, 1'b0, or_16_out);
  and SP (SP_out, multiplexer_1_out[0], multiplexer_1_out[1], multiplexer_1_out[2], multiplexer_1_out[3], 1'b1, 1'b1, ~multiplexer_1_out[6], multiplexer_1_out[7]);  // AND_Gate
  or or_18 (or_18_out, 1'b0, or_17_out);
  and CMP (COMPARE, multiplexer_1_out[0], multiplexer_1_out[1], 1'b1, 1'b1, 1'b1, 1'b1, multiplexer_1_out[6], multiplexer_1_out[7]);
  or or_19 (out_9[2], 1'b0, or_18_out);
  Multiplexer #(.width(8), .enable("false")) multiplexer_5 (
    .in0(or_3_out), .in1({4'b0000, multiplexer_1_out[5:2]}), .out(multiplexer_5_out), .sel(or_217_out));
  or or_20 (or_20_out, 1'b0, 1'b0);
  or or_21 (or_21_out, 1'b0, 1'b0);
  or or_22 (or_22_out, 1'b0, or_21_out);
  or or_23 (or_23_out, 1'b0, or_20_out);
  or or_24 (or_24_out, NAND_out, or_23_out);
  or or_25 (or_25_out, 1'b0, or_22_out);
  or or_26 (or_26_out, ADD_out, or_24_out);
  or or_27 (or_27_out, ADD_out, or_25_out);
  or or_28 (or_28_out, 1'b0, or_26_out);
  or or_29 (or_29_out, 1'b0, or_27_out);
  or or_30 (or_30_out, 1'b0, or_28_out);
  or or_31 (or_31_out, 1'b0, or_29_out);
  or or_32 (or_32_out, 1'b0, or_31_out);
  or or_33 (or_33_out, 1'b0, or_30_out);
  or or_34 (or_34_out, 1'b0, or_33_out);
  or or_35 (or_35_out, 1'b0, or_32_out);
  or or_36 (or_36_out, 1'b0, or_34_out);
  or or_37 (or_37_out, 1'b0, or_35_out);
  or or_38 (or_38_out, 1'b0, or_37_out);
  or or_39 (or_39_out, 1'b0, or_36_out);
  or or_40 (or_40_out, 1'b0, or_39_out);
  or or_41 (or_41_out, 1'b0, or_38_out);
  or or_42 (or_42_out, 1'b0, or_41_out);
  or or_43 (or_43_out, 1'b0, or_40_out);
  or or_44 (or_44_out, 1'b0, or_42_out);
  or or_45 (or_45_out, 1'b0, or_43_out);
  or or_46 (or_46_out, 1'b0, or_44_out);
  or or_47 (or_47_out, 1'b0, or_45_out);
  or or_48 (out_9[1], 1'b0, or_46_out);
  or or_49 (out_9[0], 1'b0, or_47_out);
  or or_50 (or_50_out, OR_4_out, 1'b0);
  or or_51 (or_51_out, OR_4_out, 1'b0);
  or or_52 (or_52_out, 1'b0, or_50_out);
  or or_53 (or_53_out, 1'b0, or_51_out);
  or or_54 (or_54_out, NAND_out, or_52_out);
  or or_55 (or_55_out, NAND_out, or_53_out);
  or or_56 (or_56_out, ADD_out, or_54_out);
  or or_57 (or_57_out, ADD_out, or_55_out);
  or or_58 (or_58_out, CIN_out, or_57_out);
  or or_59 (or_59_out, CIN_out, or_56_out);
  or or_60 (or_60_out, 1'b0, or_58_out);
  or or_61 (or_61_out, 1'b0, or_59_out);
  or or_62 (or_62_out, 1'b0, or_61_out);
  or or_63 (or_63_out, 1'b0, or_60_out);
  or or_64 (or_64_out, 1'b0, or_62_out);
  or or_65 (or_65_out, 1'b0, or_63_out);
  or or_66 (or_66_out, 1'b0, or_65_out);
  or or_67 (or_67_out, 1'b0, or_64_out);
  or or_68 (or_68_out, 1'b0, or_66_out);
  or or_69 (or_69_out, 1'b0, or_67_out);
  or or_70 (or_70_out, 1'b0, or_69_out);
  or or_71 (or_71_out, 1'b0, or_68_out);
  or or_72 (or_72_out, 1'b0, or_70_out);
  or or_73 (or_73_out, LB_out, or_71_out);
  or or_74 (or_74_out, 1'b0, or_72_out);
  or or_75 (or_75_out, SB_out, or_73_out);
  or or_76 (or_76_out, SP_out, or_75_out);
  or or_77 (or_77_out, 1'b0, or_74_out);
  or or_78 (or_78_out, COMPARE, or_76_out);
  or or_79 (or_79_out, COMPARE, or_77_out);
  Multiplexer #(.width(8), .enable("false")) multiplexer_6 (
    .in0(multiplexer_5_out), .in1(CUR_PC_ADDR), .out(IMM_VALUE), .sel(PCR_out));
  or or_80 (or_80_out, 1'b0, 1'b0);
  or or_81 (or_81_out, OR_4_out, 1'b0);
  or or_82 (or_82_out, 1'b0, or_80_out);
  or or_83 (or_83_out, 1'b0, or_81_out);
  or or_84 (or_84_out, 1'b0, or_82_out);
  or or_85 (or_85_out, NAND_out, or_83_out);
  or or_86 (or_86_out, 1'b0, or_84_out);
  or or_87 (or_87_out, ADD_out, or_85_out);
  or or_88 (or_88_out, CIN_out, or_87_out);
  or or_89 (or_89_out, 1'b0, or_86_out);
  or or_90 (or_90_out, 1'b0, or_88_out);
  or or_91 (or_91_out, LLI_out, or_89_out);
  or or_92 (or_92_out, 1'b0, or_90_out);
  or or_93 (or_93_out, LUI_out, or_91_out);
  or or_94 (or_94_out, 1'b0, or_93_out);
  or or_95 (or_95_out, 1'b0, or_92_out);
  or or_96 (or_96_out, 1'b0, or_94_out);
  or or_97 (or_97_out, 1'b0, or_95_out);
  or or_98 (or_98_out, POP_out, or_96_out);
  or or_99 (or_99_out, 1'b0, or_97_out);
  or or_100 (or_100_out, 1'b0, or_99_out);
  or or_101 (or_101_out, PCR_out, or_98_out);
  or or_102 (or_102_out, 1'b0, or_100_out);
  or or_103 (or_103_out, 1'b0, or_101_out);
  or or_104 (or_104_out, 1'b0, or_103_out);
  or or_105 (or_105_out, 1'b0, or_102_out);
  or or_106 (or_106_out, 1'b0, or_104_out);
  or or_107 (or_107_out, 1'b0, or_105_out);
  or or_108 (or_108_out, 1'b0, or_107_out);
  or or_109 (GPR_MUX[1], 1'b0, or_106_out);
  or or_110 (or_110_out, 1'b0, 1'b0);
  or or_111 (or_111_out, 1'b0, 1'b0);
  or or_112 (or_112_out, 1'b0, or_111_out);
  or or_113 (or_113_out, 1'b0, or_110_out);
  or or_114 (or_114_out, 1'b0, or_113_out);
  or or_115 (or_115_out, 1'b0, or_112_out);
  or or_116 (or_116_out, 1'b0, or_114_out);
  or or_117 (or_117_out, 1'b0, or_115_out);
  or or_118 (or_118_out, 1'b0, or_116_out);
  or or_119 (or_119_out, 1'b0, or_117_out);
  or or_120 (or_120_out, LLI_out, or_118_out);
  or or_121 (or_121_out, 1'b0, or_119_out);
  or or_122 (or_122_out, LUI_out, or_120_out);
  or or_123 (or_123_out, 1'b0, or_121_out);
  or or_124 (or_124_out, 1'b0, or_123_out);
  or or_125 (or_125_out, 1'b0, or_122_out);
  or or_126 (or_126_out, 1'b0, or_124_out);
  or or_127 (or_127_out, 1'b0, or_125_out);
  or or_128 (or_128_out, 1'b0, or_127_out);
  or or_129 (or_129_out, 1'b0, or_126_out);
  or or_130 (or_130_out, 1'b0, or_129_out);
  or or_131 (or_131_out, PCR_out, or_128_out);
  or or_132 (or_132_out, LB_out, or_130_out);
  or or_133 (or_133_out, LB_out, or_131_out);
  or or_134 (or_134_out, 1'b0, or_133_out);
  or or_135 (or_135_out, SB_out, or_132_out);
  or or_136 (or_136_out, 1'b0, or_135_out);
  or or_137 (or_137_out, 1'b0, or_134_out);
  or or_138 (A_MUX, 1'b0, or_136_out);
  or or_139 (GPR_MUX[0], 1'b0, or_137_out);
  Register #(.width(1), .trigger("falling")) register_3 (
    .D(JMP_FLAG), .Q(register_3_q), .clk(CLK), .clr(RST));  // open: en
  or or_140 (or_140_out, 1'b0, 1'b0);
  or or_141 (or_141_out, 1'b0, 1'b0);
  or or_142 (or_142_out, 1'b0, or_141_out);
  or or_143 (or_143_out, 1'b0, or_140_out);
  or or_144 (or_144_out, 1'b0, or_142_out);
  or or_145 (or_145_out, 1'b0, or_143_out);
  or or_146 (or_146_out, 1'b0, or_144_out);
  or or_147 (or_147_out, 1'b0, or_145_out);
  or or_148 (or_148_out, 1'b0, or_146_out);
  or or_149 (or_149_out, 1'b0, or_147_out);
  or or_150 (or_150_out, 1'b0, or_149_out);
  or or_151 (or_151_out, 1'b0, or_148_out);
  or or_152 (or_152_out, 1'b0, or_151_out);
  or or_153 (or_153_out, 1'b0, or_150_out);
  or or_154 (or_154_out, JMP_out, or_152_out);
  or or_155 (or_155_out, 1'b0, or_153_out);
  or or_156 (or_156_out, 1'b0, or_154_out);
  or or_157 (or_157_out, 1'b0, or_155_out);
  or or_158 (or_158_out, POP_out, or_157_out);
  or or_159 (or_159_out, 1'b0, or_156_out);
  or or_160 (or_160_out, 1'b0, or_159_out);
  or or_161 (or_161_out, 1'b0, or_158_out);
  or or_162 (or_162_out, 1'b0, or_161_out);
  or or_163 (or_163_out, 1'b0, or_160_out);
  or or_164 (or_164_out, 1'b0, or_162_out);
  or or_165 (or_165_out, 1'b0, or_163_out);
  or or_166 (or_166_out, 1'b0, or_164_out);
  or or_167 (or_167_out, 1'b0, or_165_out);
  or or_168 (or_168_out, 1'b0, or_167_out);
  or or_169 (POP, 1'b0, or_166_out);
  and and_2 (JMP, or_168_out, ~register_3_q);  // AND_Gate
  assign controlled_buffer_1_out = OR_4_out ? 2'b00 : 2'bz;  // Controlled_Buffer controlled_buffer_1
  or or_170 (or_170_out, 1'b0, 1'b0);
  Multiplexer #(.width(2), .enable("false")) multiplexer_7 (
    .in0(2'b00), .in1(controlled_buffer_1_out), .out(multiplexer_7_out), .sel(OR_4_out));
  assign controlled_buffer_2_out = SCO_out ? 2'b00 : 2'bz;  // Controlled_Buffer controlled_buffer_2
  or or_171 (or_171_out, 1'b0, or_170_out);
  Multiplexer #(.width(2), .enable("false")) multiplexer_8 (
    .in0(multiplexer_7_out), .in1(controlled_buffer_2_out), .out(multiplexer_8_out), .sel(SCO_out));
  assign controlled_buffer_3_out = NAND_out ? 2'b00 : 2'bz;  // Controlled_Buffer controlled_buffer_3
  or or_172 (or_172_out, 1'b0, or_171_out);
  Multiplexer #(.width(2), .enable("false")) multiplexer_9 (
    .in0(multiplexer_8_out), .in1(controlled_buffer_3_out), .out(multiplexer_9_out), .sel(NAND_out));
  assign controlled_buffer_4_out = ADD_out ? 2'b00 : 2'bz;  // Controlled_Buffer controlled_buffer_4
  Multiplexer #(.width(2), .enable("false")) multiplexer_10 (
    .in0(multiplexer_9_out), .in1(controlled_buffer_4_out), .out(multiplexer_10_out), .sel(ADD_out));
  or or_173 (or_173_out, 1'b0, or_172_out);
  assign controlled_buffer_5_out = CIN_out ? 2'b00 : 2'bz;  // Controlled_Buffer controlled_buffer_5
  or or_174 (or_174_out, 1'b0, or_173_out);
  Multiplexer #(.width(2), .enable("false")) multiplexer_11 (
    .in0(multiplexer_10_out), .in1(controlled_buffer_5_out), .out(multiplexer_11_out), .sel(CIN_out));
  assign controlled_buffer_6_out = LLI_out ? 2'b00 : 2'bz;  // Controlled_Buffer controlled_buffer_6
  Multiplexer #(.width(2), .enable("false")) multiplexer_12 (
    .in0(multiplexer_11_out), .in1(controlled_buffer_6_out), .out(multiplexer_12_out), .sel(LLI_out));
  or or_175 (or_175_out, 1'b0, or_174_out);
  assign controlled_buffer_7_out = LUI_out ? 2'b00 : 2'bz;  // Controlled_Buffer controlled_buffer_7
  Multiplexer #(.width(2), .enable("false")) multiplexer_13 (
    .in0(multiplexer_12_out), .in1(controlled_buffer_7_out), .out(multiplexer_13_out), .sel(LUI_out));
  or or_176 (or_176_out, 1'b0, or_175_out);
  assign controlled_buffer_8_out = JMP_out ? 2'b00 : 2'bz;  // Controlled_Buffer controlled_buffer_8
  or or_177 (or_177_out, 1'b0, or_176_out);
  Multiplexer #(.width(2), .enable("false")) multiplexer_14 (
    .in0(multiplexer_13_out), .in1(controlled_buffer_8_out), .out(multiplexer_14_out), .sel(JMP_out));
  assign controlled_buffer_9_out = PUSH_out ? 2'b01 : 2'bz;  // Controlled_Buffer controlled_buffer_9
  Multiplexer #(.width(2), .enable("false")) multiplexer_15 (
    .in0(multiplexer_14_out), .in1(controlled_buffer_9_out), .out(multiplexer_15_out), .sel(PUSH_out));
  or or_178 (or_178_out, PUSH_out, or_177_out);
  assign controlled_buffer_10_out = POP_out ? 2'b00 : 2'bz;  // Controlled_Buffer controlled_buffer_10
  Multiplexer #(.width(2), .enable("false")) multiplexer_16 (
    .in0(multiplexer_15_out), .in1(controlled_buffer_10_out), .out(multiplexer_16_out), .sel(POP_out));
  or or_179 (or_179_out, 1'b0, or_178_out);
  assign controlled_buffer_11_out = PCR_out ? 2'b00 : 2'bz;  // Controlled_Buffer controlled_buffer_11
  Multiplexer #(.width(2), .enable("false")) multiplexer_17 (
    .in0(multiplexer_16_out), .in1(controlled_buffer_11_out), .out(multiplexer_17_out), .sel(PCR_out));
  or or_180 (or_180_out, 1'b0, or_179_out);
  assign controlled_buffer_12_out = LB_out ? 2'b00 : 2'bz;  // Controlled_Buffer controlled_buffer_12
  or or_181 (or_181_out, 1'b0, or_180_out);
  Multiplexer #(.width(2), .enable("false")) multiplexer_18 (
    .in0(multiplexer_17_out), .in1(controlled_buffer_12_out), .out(multiplexer_18_out), .sel(LB_out));
  assign controlled_buffer_13_out = SB_out ? 2'b00 : 2'bz;  // Controlled_Buffer controlled_buffer_13
  Multiplexer #(.width(2), .enable("false")) multiplexer_19 (
    .in0(multiplexer_18_out), .in1(controlled_buffer_13_out), .out(multiplexer_19_out), .sel(SB_out));
  or or_182 (or_182_out, 1'b0, or_181_out);
  assign controlled_buffer_14_out = SP_out ? 2'b00 : 2'bz;  // Controlled_Buffer controlled_buffer_14
  Multiplexer #(.width(2), .enable("false")) multiplexer_20 (
    .in0(multiplexer_19_out), .in1(controlled_buffer_14_out), .out(multiplexer_20_out), .sel(SP_out));
  or or_183 (or_183_out, 1'b0, or_182_out);
  assign controlled_buffer_15_out = COMPARE ? 2'b00 : 2'bz;  // Controlled_Buffer controlled_buffer_15
  or or_184 (PUSH, 1'b0, or_183_out);
  Multiplexer #(.width(2), .enable("false")) multiplexer_21 (
    .in0(multiplexer_20_out), .in1(controlled_buffer_15_out), .out(multiplexer_21_out), .sel(COMPARE));
  assign A = multiplexer_2_out | multiplexer_21_out;  // OR_Gate or_185, 2 bits wide
  assign controlled_buffer_16_out = OR_4_out ? 2'b00 : 2'bz;  // Controlled_Buffer controlled_buffer_16
  assign controlled_buffer_17_out = OR_4_out ? 2'b00 : 2'bz;  // Controlled_Buffer controlled_buffer_17
  Multiplexer #(.width(2), .enable("false")) multiplexer_22 (
    .in0(2'b00), .in1(controlled_buffer_16_out), .out(multiplexer_22_out), .sel(OR_4_out));
  Multiplexer #(.width(2), .enable("false")) multiplexer_23 (
    .in0(2'b00), .in1(controlled_buffer_17_out), .out(multiplexer_23_out), .sel(OR_4_out));
  assign controlled_buffer_18_out = SCO_out ? 2'b00 : 2'bz;  // Controlled_Buffer controlled_buffer_18
  assign controlled_buffer_19_out = SCO_out ? 2'b00 : 2'bz;  // Controlled_Buffer controlled_buffer_19
  Multiplexer #(.width(2), .enable("false")) multiplexer_24 (
    .in0(multiplexer_22_out), .in1(controlled_buffer_18_out), .out(multiplexer_24_out), .sel(SCO_out));
  Multiplexer #(.width(2), .enable("false")) multiplexer_25 (
    .in0(multiplexer_23_out), .in1(controlled_buffer_19_out), .out(multiplexer_25_out), .sel(SCO_out));
  assign controlled_buffer_20_out = NAND_out ? 2'b00 : 2'bz;  // Controlled_Buffer controlled_buffer_20
  assign controlled_buffer_21_out = NAND_out ? 2'b00 : 2'bz;  // Controlled_Buffer controlled_buffer_21
  Multiplexer #(.width(2), .enable("false")) multiplexer_26 (
    .in0(multiplexer_25_out), .in1(controlled_buffer_21_out), .out(multiplexer_26_out), .sel(NAND_out));
  Multiplexer #(.width(2), .enable("false")) multiplexer_27 (
    .in0(multiplexer_24_out), .in1(controlled_buffer_20_out), .out(multiplexer_27_out), .sel(NAND_out));
  assign controlled_buffer_22_out = ADD_out ? 2'b00 : 2'bz;  // Controlled_Buffer controlled_buffer_22
  assign controlled_buffer_23_out = ADD_out ? 2'b00 : 2'bz;  // Controlled_Buffer controlled_buffer_23
  Multiplexer #(.width(2), .enable("false")) multiplexer_28 (
    .in0(multiplexer_26_out), .in1(controlled_buffer_23_out), .out(multiplexer_28_out), .sel(ADD_out));
  Multiplexer #(.width(2), .enable("false")) multiplexer_29 (
    .in0(multiplexer_27_out), .in1(controlled_buffer_22_out), .out(multiplexer_29_out), .sel(ADD_out));
  assign controlled_buffer_24_out = CIN_out ? 2'b00 : 2'bz;  // Controlled_Buffer controlled_buffer_24
  assign controlled_buffer_25_out = CIN_out ? 2'b00 : 2'bz;  // Controlled_Buffer controlled_buffer_25
  Multiplexer #(.width(2), .enable("false")) multiplexer_30 (
    .in0(multiplexer_28_out), .in1(controlled_buffer_24_out), .out(multiplexer_30_out), .sel(CIN_out));
  Multiplexer #(.width(2), .enable("false")) multiplexer_31 (
    .in0(multiplexer_29_out), .in1(controlled_buffer_25_out), .out(multiplexer_31_out), .sel(CIN_out));
  assign controlled_buffer_26_out = LLI_out ? 2'b01 : 2'bz;  // Controlled_Buffer controlled_buffer_26
  assign controlled_buffer_27_out = LLI_out ? 2'b00 : 2'bz;  // Controlled_Buffer controlled_buffer_27
  Multiplexer #(.width(2), .enable("false")) multiplexer_32 (
    .in0(multiplexer_30_out), .in1(controlled_buffer_26_out), .out(multiplexer_32_out), .sel(LLI_out));
  Multiplexer #(.width(2), .enable("false")) multiplexer_33 (
    .in0(multiplexer_31_out), .in1(controlled_buffer_27_out), .out(multiplexer_33_out), .sel(LLI_out));
  assign controlled_buffer_28_out = LUI_out ? 2'b01 : 2'bz;  // Controlled_Buffer controlled_buffer_28
  assign controlled_buffer_29_out = LUI_out ? 2'b01 : 2'bz;  // Controlled_Buffer controlled_buffer_29
  Multiplexer #(.width(2), .enable("false")) multiplexer_34 (
    .in0(multiplexer_32_out), .in1(controlled_buffer_29_out), .out(multiplexer_34_out), .sel(LUI_out));
  Multiplexer #(.width(2), .enable("false")) multiplexer_35 (
    .in0(multiplexer_33_out), .in1(controlled_buffer_28_out), .out(multiplexer_35_out), .sel(LUI_out));
  assign controlled_buffer_30_out = JMP_out ? 2'b00 : 2'bz;  // Controlled_Buffer controlled_buffer_30
  assign controlled_buffer_31_out = JMP_out ? 2'b00 : 2'bz;  // Controlled_Buffer controlled_buffer_31
  Multiplexer #(.width(2), .enable("false")) multiplexer_36 (
    .in0(multiplexer_35_out), .in1(controlled_buffer_30_out), .out(multiplexer_36_out), .sel(JMP_out));
  Multiplexer #(.width(2), .enable("false")) multiplexer_37 (
    .in0(multiplexer_34_out), .in1(controlled_buffer_31_out), .out(multiplexer_37_out), .sel(JMP_out));
  assign controlled_buffer_32_out = PUSH_out ? 2'b00 : 2'bz;  // Controlled_Buffer controlled_buffer_32
  assign controlled_buffer_33_out = PUSH_out ? 2'b00 : 2'bz;  // Controlled_Buffer controlled_buffer_33
  Multiplexer #(.width(2), .enable("false")) multiplexer_38 (
    .in0(multiplexer_37_out), .in1(controlled_buffer_32_out), .out(multiplexer_38_out), .sel(PUSH_out));
  Multiplexer #(.width(2), .enable("false")) multiplexer_39 (
    .in0(multiplexer_36_out), .in1(controlled_buffer_33_out), .out(multiplexer_39_out), .sel(PUSH_out));
  assign controlled_buffer_34_out = POP_out ? 2'b00 : 2'bz;  // Controlled_Buffer controlled_buffer_34
  assign controlled_buffer_35_out = POP_out ? 2'b01 : 2'bz;  // Controlled_Buffer controlled_buffer_35
  Multiplexer #(.width(2), .enable("false")) multiplexer_40 (
    .in0(multiplexer_38_out), .in1(controlled_buffer_35_out), .out(multiplexer_40_out), .sel(POP_out));
  Multiplexer #(.width(2), .enable("false")) multiplexer_41 (
    .in0(multiplexer_39_out), .in1(controlled_buffer_34_out), .out(multiplexer_41_out), .sel(POP_out));
  assign controlled_buffer_36_out = PCR_out ? 2'b11 : 2'bz;  // Controlled_Buffer controlled_buffer_36
  assign controlled_buffer_37_out = PCR_out ? 2'b00 : 2'bz;  // Controlled_Buffer controlled_buffer_37
  Multiplexer #(.width(2), .enable("false")) multiplexer_42 (
    .in0(multiplexer_40_out), .in1(controlled_buffer_36_out), .out(multiplexer_42_out), .sel(PCR_out));
  Multiplexer #(.width(2), .enable("false")) multiplexer_43 (
    .in0(multiplexer_41_out), .in1(controlled_buffer_37_out), .out(multiplexer_43_out), .sel(PCR_out));
  assign controlled_buffer_38_out = LB_out ? 2'b00 : 2'bz;  // Controlled_Buffer controlled_buffer_38
  assign controlled_buffer_39_out = LB_out ? 2'b00 : 2'bz;  // Controlled_Buffer controlled_buffer_39
  Multiplexer #(.width(2), .enable("false")) multiplexer_44 (
    .in0(multiplexer_42_out), .in1(controlled_buffer_38_out), .out(multiplexer_44_out), .sel(LB_out));
  Multiplexer #(.width(2), .enable("false")) multiplexer_45 (
    .in0(multiplexer_43_out), .in1(controlled_buffer_39_out), .out(multiplexer_45_out), .sel(LB_out));
  assign controlled_buffer_40_out = SB_out ? 2'b00 : 2'bz;  // Controlled_Buffer controlled_buffer_40
  assign controlled_buffer_41_out = SB_out ? 2'b00 : 2'bz;  // Controlled_Buffer controlled_buffer_41
  Multiplexer #(.width(2), .enable("false")) multiplexer_46 (
    .in0(multiplexer_45_out), .in1(controlled_buffer_41_out), .out(multiplexer_46_out), .sel(SB_out));
  Multiplexer #(.width(2), .enable("false")) multiplexer_47 (
    .in0(multiplexer_44_out), .in1(controlled_buffer_40_out), .out(multiplexer_47_out), .sel(SB_out));
  assign controlled_buffer_42_out = SP_out ? 2'b00 : 2'bz;  // Controlled_Buffer controlled_buffer_42
  assign controlled_buffer_43_out = SP_out ? 2'b00 : 2'bz;  // Controlled_Buffer controlled_buffer_43
  Multiplexer #(.width(2), .enable("false")) multiplexer_48 (
    .in0(multiplexer_47_out), .in1(controlled_buffer_42_out), .out(multiplexer_48_out), .sel(SP_out));
  Multiplexer #(.width(2), .enable("false")) multiplexer_49 (
    .in0(multiplexer_46_out), .in1(controlled_buffer_43_out), .out(multiplexer_49_out), .sel(SP_out));
  assign controlled_buffer_44_out = COMPARE ? 2'b00 : 2'bz;  // Controlled_Buffer controlled_buffer_44
  assign controlled_buffer_45_out = COMPARE ? 2'b00 : 2'bz;  // Controlled_Buffer controlled_buffer_45
  Multiplexer #(.width(2), .enable("false")) multiplexer_50 (
    .in0(multiplexer_48_out), .in1(controlled_buffer_45_out), .out(multiplexer_50_out), .sel(COMPARE));
  Multiplexer #(.width(2), .enable("false")) multiplexer_51 (
    .in0(multiplexer_49_out), .in1(controlled_buffer_44_out), .out(multiplexer_51_out), .sel(COMPARE));
  Multiplexer #(.width(2), .enable("false")) multiplexer_52 (
    .in0(multiplexer_4_out), .in1(multiplexer_3_out), .out(multiplexer_52_out), .sel(LB_out));
  assign B = multiplexer_3_out | multiplexer_51_out;  // OR_Gate or_186, 2 bits wide
  assign C = multiplexer_52_out | multiplexer_50_out;  // OR_Gate or_187, 2 bits wide
  or or_188 (or_188_out, 1'b0, 1'b0);
  or or_189 (or_189_out, 1'b0, 1'b0);
  or or_190 (or_190_out, 1'b0, or_188_out);
  or or_191 (or_191_out, 1'b0, or_189_out);
  or or_192 (or_192_out, 1'b0, or_190_out);
  or or_193 (or_193_out, 1'b0, or_191_out);
  or or_194 (or_194_out, 1'b0, or_193_out);
  or or_195 (or_195_out, 1'b0, or_192_out);
  or or_196 (or_196_out, 1'b0, or_194_out);
  or or_197 (or_197_out, 1'b0, or_195_out);
  or or_198 (or_198_out, 1'b0, or_197_out);
  or or_199 (or_199_out, LLI_out, or_196_out);
  or or_200 (or_200_out, 1'b0, or_198_out);
  or or_201 (or_201_out, 1'b0, or_199_out);
  or or_202 (or_202_out, 1'b0, or_200_out);
  or or_203 (or_203_out, 1'b0, or_201_out);
  or or_204 (or_204_out, 1'b0, or_202_out);
  or or_205 (or_205_out, 1'b0, or_203_out);
  or or_206 (or_206_out, 1'b0, or_205_out);
  or or_207 (or_207_out, 1'b0, or_204_out);
  or or_208 (or_208_out, 1'b0, or_207_out);
  or or_209 (or_209_out, 1'b0, or_206_out);
  or or_210 (or_210_out, 1'b0, or_209_out);
  or or_211 (or_211_out, 1'b0, or_208_out);
  or or_212 (or_212_out, 1'b0, or_211_out);
  or or_213 (or_213_out, 1'b0, or_210_out);
  or or_214 (or_214_out, 1'b0, or_213_out);
  or or_215 (or_215_out, SP_out, or_212_out);
  or or_216 (or_216_out, 1'b0, or_215_out);
  or or_217 (or_217_out, 1'b0, or_214_out);
  or or_218 (or_218_out, 1'b0, 1'b0);
  or or_219 (or_219_out, 1'b0, or_218_out);
  or or_220 (or_220_out, 1'b0, or_219_out);
  or or_221 (or_221_out, 1'b0, or_220_out);
  or or_222 (or_222_out, 1'b0, or_221_out);
  or or_223 (or_223_out, 1'b0, or_222_out);
  or or_224 (or_224_out, 1'b0, or_223_out);
  or or_225 (or_225_out, 1'b0, or_224_out);
  or or_226 (or_226_out, 1'b0, or_225_out);
  or or_227 (or_227_out, 1'b0, or_226_out);
  or or_228 (or_228_out, 1'b0, or_227_out);
  or or_229 (or_229_out, 1'b0, or_228_out);
  or or_230 (or_230_out, SB_out, or_229_out);
  or or_231 (or_231_out, 1'b0, or_230_out);
  or or_232 (out_16, 1'b0, or_231_out);
  or or_233 (or_233_out, LB_out, SB_out);
  and and_3 (and_3_out, SCO_out, ~register_5_q, CLK);  // AND_Gate
  or or_234 (or_234_out, or_233_out, or_168_out);
  Register #(.width(4), .trigger("falling")) register_4 (
    .D(multiplexer_1_out[7:4]), .Q(AUX_OP), .clk(and_3_out), .clr(RST));  // open: en
  Register #(.width(1), .trigger("falling")) register_5 (
    .D(or_234_out), .Q(register_5_q), .clk(CLK), .clr(RST));  // open: en

  // Notes on the sheet:
  //   DATA
  //   ALU OPCODE
  //   WRITE ENABLE
endmodule

module STK (
  input  [7:0] in_1,
  input  in_2,
  input  in_3,
  input  in_4,
  input  in_5,
  output [7:0] out_6
);

  wire and_1_out, or_1_out;
  wire [7:0] multiplexer_1_out, multiplexer_2_out, multiplexer_3_out, multiplexer_4_out, multiplexer_5_out,
       multiplexer_6_out, multiplexer_7_out, multiplexer_8_out, multiplexer_9_out, multiplexer_10_out,
       multiplexer_11_out, multiplexer_12_out, multiplexer_13_out, multiplexer_14_out, multiplexer_15_out,
       multiplexer_16_out, multiplexer_17_out, multiplexer_18_out, multiplexer_19_out, multiplexer_20_out,
       multiplexer_21_out, multiplexer_22_out, multiplexer_23_out, multiplexer_24_out, multiplexer_25_out,
       multiplexer_26_out, multiplexer_27_out, multiplexer_28_out, multiplexer_29_out, multiplexer_30_out,
       multiplexer_31_out, multiplexer_32_out, register_2_q, register_3_q, register_4_q, register_5_q,
       register_6_q, register_7_q, register_8_q, register_9_q, register_10_q, register_11_q, register_12_q,
       register_13_q, register_14_q, register_15_q, register_16_q, register_17_q, register_18_q,
       register_19_q, register_20_q, register_21_q, register_22_q, register_23_q, register_24_q,
       register_25_q, register_26_q, register_27_q, register_28_q, register_29_q, register_30_q,
       register_31_q, register_32_q;

  and and_1 (and_1_out, in_2, or_1_out);
  or or_1 (or_1_out, in_4, in_5);
  Multiplexer #(.width(8), .enable("false")) multiplexer_1 (
    .in0(register_2_q), .in1(in_1), .out(multiplexer_1_out), .sel(in_5));
  Multiplexer #(.width(8), .enable("false")) multiplexer_2 (
    .in0(register_3_q), .in1(out_6), .out(multiplexer_2_out), .sel(in_5));
  Register register_1 (.D(multiplexer_1_out), .Q(out_6), .clk(and_1_out), .clr(in_3));  // open: en
  Register register_2 (.D(multiplexer_2_out), .Q(register_2_q), .clk(and_1_out), .clr(in_3));  // open: en
  Multiplexer #(.width(8), .enable("false")) multiplexer_3 (
    .in0(register_4_q), .in1(register_2_q), .out(multiplexer_3_out), .sel(in_5));
  Register register_3 (.D(multiplexer_3_out), .Q(register_3_q), .clk(and_1_out), .clr(in_3));  // open: en
  Multiplexer #(.width(8), .enable("false")) multiplexer_4 (
    .in0(register_5_q), .in1(register_3_q), .out(multiplexer_4_out), .sel(in_5));
  Register register_4 (.D(multiplexer_4_out), .Q(register_4_q), .clk(and_1_out), .clr(in_3));  // open: en
  Multiplexer #(.width(8), .enable("false")) multiplexer_5 (
    .in0(register_6_q), .in1(register_4_q), .out(multiplexer_5_out), .sel(in_5));
  Register register_5 (.D(multiplexer_5_out), .Q(register_5_q), .clk(and_1_out), .clr(in_3));  // open: en
  Multiplexer #(.width(8), .enable("false")) multiplexer_6 (
    .in0(register_7_q), .in1(register_5_q), .out(multiplexer_6_out), .sel(in_5));
  Multiplexer #(.width(8), .enable("false")) multiplexer_7 (
    .in0(register_8_q), .in1(register_6_q), .out(multiplexer_7_out), .sel(in_5));
  Register register_6 (.D(multiplexer_6_out), .Q(register_6_q), .clk(and_1_out), .clr(in_3));  // open: en
  Register register_7 (.D(multiplexer_7_out), .Q(register_7_q), .clk(and_1_out), .clr(in_3));  // open: en
  Multiplexer #(.width(8), .enable("false")) multiplexer_8 (
    .in0(register_9_q), .in1(register_7_q), .out(multiplexer_8_out), .sel(in_5));
  Register register_8 (.D(multiplexer_8_out), .Q(register_8_q), .clk(and_1_out), .clr(in_3));  // open: en
  Multiplexer #(.width(8), .enable("false")) multiplexer_9 (
    .in0(register_10_q), .in1(register_8_q), .out(multiplexer_9_out), .sel(in_5));
  Multiplexer #(.width(8), .enable("false")) multiplexer_10 (
    .in0(register_11_q), .in1(register_9_q), .out(multiplexer_10_out), .sel(in_5));
  Register register_9 (.D(multiplexer_9_out), .Q(register_9_q), .clk(and_1_out), .clr(in_3));  // open: en
  Register register_10 (.D(multiplexer_10_out), .Q(register_10_q), .clk(and_1_out), .clr(in_3));  // open: en
  Multiplexer #(.width(8), .enable("false")) multiplexer_11 (
    .in0(register_12_q), .in1(register_10_q), .out(multiplexer_11_out), .sel(in_5));
  Register register_11 (.D(multiplexer_11_out), .Q(register_11_q), .clk(and_1_out), .clr(in_3));  // open: en
  Multiplexer #(.width(8), .enable("false")) multiplexer_12 (
    .in0(register_13_q), .in1(register_11_q), .out(multiplexer_12_out), .sel(in_5));
  Register register_12 (.D(multiplexer_12_out), .Q(register_12_q), .clk(and_1_out), .clr(in_3));  // open: en
  Multiplexer #(.width(8), .enable("false")) multiplexer_13 (
    .in0(register_14_q), .in1(register_12_q), .out(multiplexer_13_out), .sel(in_5));
  Register register_13 (.D(multiplexer_13_out), .Q(register_13_q), .clk(and_1_out), .clr(in_3));  // open: en
  Multiplexer #(.width(8), .enable("false")) multiplexer_14 (
    .in0(register_15_q), .in1(register_13_q), .out(multiplexer_14_out), .sel(in_5));
  Multiplexer #(.width(8), .enable("false")) multiplexer_15 (
    .in0(register_16_q), .in1(register_14_q), .out(multiplexer_15_out), .sel(in_5));
  Register register_14 (.D(multiplexer_14_out), .Q(register_14_q), .clk(and_1_out), .clr(in_3));  // open: en
  Register register_15 (.D(multiplexer_15_out), .Q(register_15_q), .clk(and_1_out), .clr(in_3));  // open: en
  Multiplexer #(.width(8), .enable("false")) multiplexer_16 (
    .in0(register_17_q), .in1(register_15_q), .out(multiplexer_16_out), .sel(in_5));
  Register register_16 (.D(multiplexer_16_out), .Q(register_16_q), .clk(and_1_out), .clr(in_3));  // open: en
  Multiplexer #(.width(8), .enable("false")) multiplexer_17 (
    .in0(register_18_q), .in1(register_16_q), .out(multiplexer_17_out), .sel(in_5));
  Multiplexer #(.width(8), .enable("false")) multiplexer_18 (
    .in0(register_19_q), .in1(register_17_q), .out(multiplexer_18_out), .sel(in_5));
  Register register_17 (.D(multiplexer_17_out), .Q(register_17_q), .clk(and_1_out), .clr(in_3));  // open: en
  Register register_18 (.D(multiplexer_18_out), .Q(register_18_q), .clk(and_1_out), .clr(in_3));  // open: en
  Multiplexer #(.width(8), .enable("false")) multiplexer_19 (
    .in0(register_20_q), .in1(register_18_q), .out(multiplexer_19_out), .sel(in_5));
  Register register_19 (.D(multiplexer_19_out), .Q(register_19_q), .clk(and_1_out), .clr(in_3));  // open: en
  Multiplexer #(.width(8), .enable("false")) multiplexer_20 (
    .in0(register_21_q), .in1(register_19_q), .out(multiplexer_20_out), .sel(in_5));
  Register register_20 (.D(multiplexer_20_out), .Q(register_20_q), .clk(and_1_out), .clr(in_3));  // open: en
  Multiplexer #(.width(8), .enable("false")) multiplexer_21 (
    .in0(register_22_q), .in1(register_20_q), .out(multiplexer_21_out), .sel(in_5));
  Register register_21 (.D(multiplexer_21_out), .Q(register_21_q), .clk(and_1_out), .clr(in_3));  // open: en
  Multiplexer #(.width(8), .enable("false")) multiplexer_22 (
    .in0(register_23_q), .in1(register_21_q), .out(multiplexer_22_out), .sel(in_5));
  Multiplexer #(.width(8), .enable("false")) multiplexer_23 (
    .in0(register_24_q), .in1(register_22_q), .out(multiplexer_23_out), .sel(in_5));
  Register register_22 (.D(multiplexer_22_out), .Q(register_22_q), .clk(and_1_out), .clr(in_3));  // open: en
  Register register_23 (.D(multiplexer_23_out), .Q(register_23_q), .clk(and_1_out), .clr(in_3));  // open: en
  Multiplexer #(.width(8), .enable("false")) multiplexer_24 (
    .in0(register_25_q), .in1(register_23_q), .out(multiplexer_24_out), .sel(in_5));
  Register register_24 (.D(multiplexer_24_out), .Q(register_24_q), .clk(and_1_out), .clr(in_3));  // open: en
  Multiplexer #(.width(8), .enable("false")) multiplexer_25 (
    .in0(register_26_q), .in1(register_24_q), .out(multiplexer_25_out), .sel(in_5));
  Multiplexer #(.width(8), .enable("false")) multiplexer_26 (
    .in0(register_27_q), .in1(register_25_q), .out(multiplexer_26_out), .sel(in_5));
  Register register_25 (.D(multiplexer_25_out), .Q(register_25_q), .clk(and_1_out), .clr(in_3));  // open: en
  Register register_26 (.D(multiplexer_26_out), .Q(register_26_q), .clk(and_1_out), .clr(in_3));  // open: en
  Multiplexer #(.width(8), .enable("false")) multiplexer_27 (
    .in0(register_28_q), .in1(register_26_q), .out(multiplexer_27_out), .sel(in_5));
  Register register_27 (.D(multiplexer_27_out), .Q(register_27_q), .clk(and_1_out), .clr(in_3));  // open: en
  Multiplexer #(.width(8), .enable("false")) multiplexer_28 (
    .in0(register_29_q), .in1(register_27_q), .out(multiplexer_28_out), .sel(in_5));
  Register register_28 (.D(multiplexer_28_out), .Q(register_28_q), .clk(and_1_out), .clr(in_3));  // open: en
  Multiplexer #(.width(8), .enable("false")) multiplexer_29 (
    .in0(register_30_q), .in1(register_28_q), .out(multiplexer_29_out), .sel(in_5));
  Register register_29 (.D(multiplexer_29_out), .Q(register_29_q), .clk(and_1_out), .clr(in_3));  // open: en
  Multiplexer #(.width(8), .enable("false")) multiplexer_30 (
    .in0(register_31_q), .in1(register_29_q), .out(multiplexer_30_out), .sel(in_5));
  Multiplexer #(.width(8), .enable("false")) multiplexer_31 (
    .in0(register_32_q), .in1(register_30_q), .out(multiplexer_31_out), .sel(in_5));
  Register register_30 (.D(multiplexer_30_out), .Q(register_30_q), .clk(and_1_out), .clr(in_3));  // open: en
  Register register_31 (.D(multiplexer_31_out), .Q(register_31_q), .clk(and_1_out), .clr(in_3));  // open: en
  Multiplexer #(.width(8), .enable("false")) multiplexer_32 (
    .in0({8{1'b0}}), .in1(register_31_q), .out(multiplexer_32_out), .sel(in_5));
  Register register_32 (.D(multiplexer_32_out), .Q(register_32_q), .clk(and_1_out), .clr(in_3));  // open: en
endmodule

module PC (
  input  [7:0] Jump_Address,
  input  Jump_Enable,
  input  in_3,
  input  in_4,
  input  in_5,
  output [7:0] out_6,
  output [7:0] out_7
);

  wire not_1_out;
  wire [7:0] multiplexer_1_out;

  Multiplexer #(.width(8), .enable("false")) multiplexer_1 (
    .in0(out_7), .in1(Jump_Address), .out(multiplexer_1_out), .sel(Jump_Enable));
  not not_1 (not_1_out, in_3);
  Register #(.trigger("falling")) register_1 (.D(multiplexer_1_out), .en(not_1_out), .Q(out_6), .clk(in_4), .clr(in_5));
  Adder adder_1 (.a(out_6), .b(8'h1), .out(out_7));  // open: cin, cout
endmodule

module _7SegDisplay (
  input  [7:0] in_1,
  input  Reset,
  output [7:0] Address
);

  wire clock_1_out, comparator_1_eq;
  wire [7:0] mcu_1_out, register_1_q;

  MCU mcu_1 (.IN_ENABLE(comparator_1_eq), .IN(in_1), .ADDR(Address), .OUT(mcu_1_out), .CLK(clock_1_out), .RST(Reset));
  Clock clock_1 (.out(clock_1_out));
  Comparator #(.mode("unsigned")) comparator_1 (.a({8{1'b1}}), .b(Address), .eq(comparator_1_eq));  // open: gt, lt
  Hex_Digit_Display hex_digit_display_1 (.value(register_1_q[7:4]));  // open: dp
  Register register_1 (.D(mcu_1_out), .en(comparator_1_eq), .Q(register_1_q), .clk(clock_1_out), .clr(Reset));
  Hex_Digit_Display hex_digit_display_2 (.value(register_1_q[3:0]));  // open: dp
endmodule
